# Fritzing sketch PIA (saved by Fritzing 0.9.3b)
breadboards: 1

parts:
  Part1 = Arduino Mega ADK (Rev3)  # not connected
  LED4 = LED - 5mm [color="Red (633nm)" package="5 mm [THT]"]  # not connected
  LED5 = LED - 5mm [color="Yellow (595nm)" package="5 mm [THT]"]  # not connected
  LED6 = LED - 5mm [color="Green (570nm)" package="5 mm [THT]"]  # not connected
  LED7 = LED - 5mm [color="Red (633nm)" package="5 mm [THT]"]  # not connected
  LED8 = LED - 5mm [color="Yellow (595nm)" package="5 mm [THT]"]  # not connected
  LED9 = LED - 5mm [color="Green (570nm)" package="5 mm [THT]"]  # not connected
  R2 = Resistor [tolerance=±5% resistance=220 package="2010 [SMD]"]
  R3 = Resistor [tolerance=±5% resistance=220 package="2010 [SMD]"]
  R4 = Resistor [tolerance=±5% resistance=220 package="2010 [SMD]"]
  R5 = Resistor [tolerance=±5% resistance=220 package="2010 [SMD]"]
  R6 = Resistor [tolerance=±5% resistance=220 package="2010 [SMD]"]
  R7 = Resistor [tolerance=±5% resistance=220 package="2010 [SMD]"]
  S2 = Pushbutton [package="[THT]"]

nets:
  N1: R2.Pin_1, R3.Pin_1, R4.Pin_1, R5.Pin_1, R6.Pin_1, R7.Pin_1
  N2: S2.Pin_1, S2.Pin_2
  N3: S2.Pin_3, S2.Pin_4

// code stored in the sketch: semaforo.ino
// Pines de arduino
int green1 = 5
int yellow1 = 6
int red1 = 7
int green2 = 8
int yellow2 = 9
int red2 = 10

void turnoff(led){
  // Apaga LED
  digitalWrite(led, LOW);
}
void turnon(led){
  // Prende LED
  digitalWrite(led, HIGH);
}
void switchled(ledoff,ledon,wait){
  // Apaga un led, prende otro y espera <wait> milisegundos
  turnoff(ledoff);
  turnon(ledon);
  sleep(wait);
}
void green2red(green,yellow,red){
  // Secuencia de verde a amarillo a rojo
  switchled(red,green,5000);
  switchled(green,yellow,1500);
  switchled(yellow,red,500);
}
void main(){
  // Define estado inicial e inicia secuencia de transformación de LEDs
  turnon(green1);
  turnon(red2);
  green2red(green1,yellow1,red1);
  green2red(green2,yellow2,red2);
}
void loop(){
  // Inicia programa en loop indefinidamente
  main();
}
